# Fritzing sketch Noise_D-ffx3_XNOR (saved by Fritzing 0.9.4)
breadboards: 1

parts:
  IC1 = IC, DIP package, 20 pins [chip_label="74HC574\n"]
  C1 = Ceramic Capacitor [capacitance=100nF package="100 mil [THT, multilayer]"]
  IC2 = IC, DIP package, 20 pins [chip_label="74HC574\n"]
  C2 = Ceramic Capacitor [capacitance=100nF package="100 mil [THT, multilayer]"]
  C3 = Film/Foil Capacitor [capacitance=100nF voltage=35V package="5mm [THT, pp]"]
  IC3 = IC, DIP package, 14 pins [chip_label=74HC86]
  C4 = Ceramic Capacitor [capacitance=100nF package="100 mil [THT, multilayer]"]
  C5 = Electrolytic Capacitor [capacitance=1µF package="100 mil [THT, electrolytic]"]
  IC4 = IC, DIP package, 20 pins [chip_label="74HC574\n"]
  C6 = Ceramic Capacitor [capacitance=100nF package="100 mil [THT, multilayer]"]
  R2 = Resistor [tolerance=±5% resistance=150 package=THT]

nets:
  N1: IC1.pin1, IC1.pin10, C1.1, IC2.pin1, IC2.pin10, C2.1, C3.-, C3.+, IC3.pin7, IC3.pin9, IC3.pin10, IC3.pin12, IC3.pin13, C4.1, C5.-, IC4.pin1, IC4.pin10, C6.1, R2.Pin_1
  N2: IC1.pin2, IC3.pin6
  N3: IC1.pin3, IC1.pin19
  N4: IC1.pin4, IC1.pin18
  N5: IC1.pin5, IC1.pin17
  N6: IC1.pin6, IC1.pin16
  N7: IC1.pin7, IC1.pin15
  N8: IC1.pin8, IC1.pin14
  N9: IC1.pin9, IC1.pin13
  N10: IC1.pin11, IC2.pin11, IC4.pin11
  N11: IC1.pin12, IC2.pin2
  N12: IC1.pin20, C1.0, IC2.pin20, C2.0, IC3.pin4, IC3.pin14, C4.0, C5.+, IC4.pin20, C6.0
  N13: IC2.pin3, IC2.pin19
  N14: IC2.pin4, IC2.pin18
  N15: IC2.pin5, IC2.pin17
  N16: IC2.pin6, IC2.pin16
  N17: IC2.pin7, IC2.pin15
  N18: IC2.pin8, IC2.pin14
  N19: IC2.pin9, IC2.pin13
  N20: IC2.pin12, IC4.pin2
  N21: IC3.pin1, IC4.pin8, IC4.pin14
  N22: IC3.pin2, IC4.pin7, IC4.pin15
  N23: IC3.pin3, IC3.pin5
  N24: IC4.pin3, IC4.pin19
  N25: IC4.pin4, IC4.pin18
  N26: IC4.pin5, IC4.pin17
  N27: IC4.pin6, IC4.pin16
  N28: IC4.pin9, IC4.pin13
  N29: IC4.pin12, R2.Pin_0

notes:
  74HC574 D-FF
  1 !OE 20 VCC
  2 1D 19 1Q
  3 2D 18 2Q
  4 3D 17 3Q
  5 4D 16 4Q
  6 5D 15 5Q
  7 6D 14 6Q
  8 7D 13 7Q
  9 8D 12 8Q
  10 GND 11 CLK
  100kHz
  Clk
  OUTPUT
  74HC86 XOR
  1 1A 14 VCC
  2 1B 13 4B
  3 1Y 12 4A
  4 2A 11 4Y
  5 2B 10 3B
  6 2Y 9 3A
  7 GND 8 3Y
  GND
  +5V
  C=0.1uF R=150Ω
  fc ≒ 10.6kHz
