# Fritzing sketch Noise_Inverter (saved by Fritzing 0.9.4)
breadboards: 2

parts:
  IC1 = IC, DIP package, 14 pins [chip_label=TC4069]
  R1 = Resistor [tolerance=±5% resistance=1M package=THT]
  C1 = Film/Foil Capacitor [capacitance=100nF voltage=35V package="5mm [THT, pp]"]
  R2 = Resistor [tolerance=±5% resistance=1M package=THT]
  C2 = Film/Foil Capacitor [capacitance=100nF voltage=35V package="5mm [THT, pp]"]
  R3 = Resistor [tolerance=±5% resistance=1M package=THT]
  C4 = Film/Foil Capacitor [capacitance=100nF voltage=35V package="5mm [THT, pp]"]
  R4 = Resistor [tolerance=±5% resistance=1M package=THT]
  C5 = Film/Foil Capacitor [capacitance=100nF voltage=35V package="5mm [THT, pp]"]
  R5 = Resistor [tolerance=±5% resistance=1M package=THT]
  C6 = Electrolytic Capacitor [capacitance=1µF package="100 mil [THT, electrolytic]"]
  C7 = Ceramic Capacitor [capacitance=100nF package="100 mil [THT, multilayer]"]

nets:
  N1: IC1.pin1, R1.Pin_0
  N2: IC1.pin2, R1.Pin_1, C1.+
  N3: IC1.pin3, C1.-, R2.Pin_0
  N4: IC1.pin4, R2.Pin_1, C2.+
  N5: IC1.pin5, C2.-, R3.Pin_0
  N6: IC1.pin9, IC1.pin10, R5.Pin_1
  N7: IC1.pin11, C5.+, R5.Pin_0
  N8: IC1.pin12, R4.Pin_0, C5.-
  N9: IC1.pin13, C4.-, R4.Pin_1
  N10: IC1.pin14, C6.+, C7.0
  N11: R3.Pin_1, C4.+
  N12: C6.-, C7.1

notes:
  OUT
  GND
  +5V
  GND
  NC
