# Fritzing sketch Noise_SinthDIY_ECB (saved by Fritzing 0.9.4)
breadboards: 1

parts:
  Q1 = NPN-Transistor [package="TO92 [THT]"]
  R1 = Resistor [tolerance=±5% resistance=1M package=THT]
  C1 = Film/Foil Capacitor [capacitance=100nF voltage=35V package="5mm [THT, pp]"]
  Q2 = NPN-Transistor [package="TO92 [THT]"]
  R2 = Resistor [tolerance=±5% resistance=2.2M package=THT]
  R3 = Resistor [tolerance=±5% resistance=4.7k package=THT]
  C4 = Film/Foil Capacitor [capacitance=100nF voltage=35V package="5mm [THT, pp]"]
  C5 = Electrolytic Capacitor [capacitance=1µF package="100 mil [THT, electrolytic]"]
  R4 = Resistor [tolerance=±5% resistance=100k package=THT]

nets:
  N1: Q1.E, R1.Pin_1, C1.-
  N2: Q1.C, Q2.E, C5.-, R4.Pin_0
  N3: R1.Pin_0, R3.Pin_0, C5.+
  N4: C1.+, Q2.C, R2.Pin_0
  N5: Q2.B, R2.Pin_1, R3.Pin_1, C4.-
  N6: C4.+, R4.Pin_1

notes:
  GND
  +12V
  NPN-ECB
  OUT
