# Fritzing sketch Noise_improved_ECB (saved by Fritzing 0.9.4)
breadboards: 1

parts:
  Q1 = NPN-Transistor [package="TO92 [THT]"]
  R1 = Resistor [tolerance=±5% resistance=680k package=THT]
  C1 = Film/Foil Capacitor [capacitance=100nF voltage=35V package="5mm [THT, pp]"]
  Q2 = NPN-Transistor [package="TO92 [THT]"]
  R2 = Resistor [tolerance=±5% resistance=4.7k package=THT]
  R3 = Resistor [tolerance=±5% resistance=1k package=THT]
  C2 = Electrolytic Capacitor [capacitance=1µF package="100 mil [THT, electrolytic]"]
  R4 = Resistor [tolerance=±5% resistance=100k package=THT]
  C4 = Electrolytic Capacitor [capacitance=1µF package="100 mil [THT, electrolytic]"]
  C5 = Film/Foil Capacitor [capacitance=100nF voltage=35V package="5mm [THT, pp]"]

nets:
  N1: Q1.E, R1.Pin_1, C1.-
  N2: Q1.C, Q2.C
  N3: R1.Pin_0, C1.+, R2.Pin_0, C4.-
  N4: Q2.E, R3.Pin_0, C2.+
  N5: Q2.B, R2.Pin_1, C5.-
  N6: R3.Pin_1, C2.-, R4.Pin_0, C4.+
  N7: R4.Pin_1, C5.+

notes:
  OUT
  GND
  +12V
  GND
  NC
